# Fritzing sketch PyPiBot (saved by Fritzing 0.9.2b)
breadboards: 1

parts:
  Raspberry_Pi1 = Raspberry Pi B+
  M1 = DC Motor
  MD03A1 = Dual VNH2SP30 Motor Driver [part_number=MD03A]
  VCC1 = 4 x AAA Battery Mount
  IC1 = Voltage Regulator [package=to-220-alt]

nets:
  N1: Raspberry_Pi1.GPIO2, MD03A1.PWM
  N2: Raspberry_Pi1.GPIO3, MD03A1.1INb
  N3: Raspberry_Pi1.GPIO4, MD03A1.1INa
  GND: Raspberry_Pi1.GND, MD03A1.GND, VCC1.-, IC1.IN
  N4: Raspberry_Pi1.5V, MD03A1.+5V_(IN), IC1.OUT
  N5: M1.pin_1, MD03A1.OUT_1A
  N6: M1.pin_2, MD03A1.OUT_1B
  VIN: MD03A1.VIN, VCC1.+, IC1.GND
